# Fritzing sketch CarOpenerWiring (saved by Fritzing 0.9.3b)
breadboards: 1
perfboards: 1

parts:
  BUZZER = Buzzer 12mm [package=buzzer-12mm-ns]
  5VDC-3_3VDC_CONVERTER = Step Down 5V to 3.3V [package="DIP (Dual Inline) [THT]"]
  LED1 = LED - 3mm [color="Green (555nm)" package="3 mm [THT]"]
  LED2 = LED - 3mm [color="Red (633nm)" package="3 mm [THT]"]
  LED3 = LED - 3mm [color="Blue (430nm)" package="3 mm [THT]"]
  R2 = Resistor [tolerance=±5% resistance=220 package="2010 [SMD]"]
  X1 = USB Connectors [package=usb-a-s-nosilk-female]
  S2 = Toggle Switch [package=THT]
  R3 = Resistor [tolerance=±5% resistance=220 package="2010 [SMD]"]
  R4 = Resistor [tolerance=±5% resistance=220 package="2010 [SMD]"]
  U1 = ESP32S-HiLetgo [part_number=ESP32S-HiLetgo]
  S3 = Pushbutton [package="[THT]"]
  S4 = Pushbutton [package="[THT]"]
  S5 = Pushbutton [package="[THT]"]
  LED4 = LEDs [package=fkit-led-1206]  # not connected
  C2 = Capacitor [package=grm43d]  # not connected
  2_RELAYS = 2-Channel 5v Relay Shield [package=relay-2ch5v10a]

nets:
  N1: BUZZER.1, U1.GPIO13
  GND: BUZZER.2, 5VDC-3_3VDC_CONVERTER.GND, LED1.cathode, LED2.cathode, LED3.cathode, X1.GND, S2.L1, U1.GND, 2_RELAYS.GND
  VIN: 5VDC-3_3VDC_CONVERTER.IN, X1.VBUS, U1.VIN, 2_RELAYS.VCC
  N2: LED1.anode, R2.Pin_0
  N3: LED2.anode, R3.Pin_0
  N4: LED3.anode, R4.Pin_0
  N5: R2.Pin_1, U1.GPIO2
  N6: S2.L2, R4.Pin_1, U1.3.3
  N7: R3.Pin_1, U1.GPIO4
  N8: U1.GPIO22, 2_RELAYS.IN2
  N9: U1.GPIO23, 2_RELAYS.IN1
  N10: S3.Pin_1, S3.Pin_2, 2_RELAYS.K1-On
  N11: S3.Pin_3, S3.Pin_4
  N12: S4.Pin_1, S4.Pin_2
  N13: S4.Pin_3, S4.Pin_4
  N14: S5.Pin_1, S5.Pin_2, 2_RELAYS.K2-On
  N15: S5.Pin_3, S5.Pin_4

custom parts:
  Step Down 5V to 3.3V: Step Down 5V to 3.3V 1A
  ESP32S-HiLetgo: HiLetgo ESP-WROOM-32 ESP32 ESP-32S Development Board 2.4GHz Dual-Mode WiFi + Bluetooth Dual Cores Microcontroller The ESP32 integrated with Antenna switches, RF Balun, power amplifiers, low-noise amplifiers, filters, and management modules, and the entire solution occupies the least area of PCB. 2.4 GHz Wi-Fi plus Bluetooth dual-mode chip, with TSMC Ultra-low power consumption 40nm technology,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
  2-Channel 5v Relay Shield: 2 Channel 5v Relay Shield w. 2x SPD-06VDC-SD-C
